// Logisim project ALU.circ as structural Verilog: 3 circuits, main circuit ALU
module ALU (
  input  [31:0] op1,
  input  [31:0] op2,
  input  [5:0] ALU_opcode,
  input  [4:0] shift_amt,
  input  clk,
  input  rst,
  output [31:0] ALU_res,
  output zero_flag,
  output overflow_flag,
  output carry_out
);

  wire add_c, add_v, and_4_out, and_5_out, comparator_1_lt, comparator_2_lt, comparator_6_eq, hi_en, lo_en,
       mthi, mtlo, mult, multiplexer_7_out, not_1_out, or_3_out, sub_c, sub_v;
  wire [31:0] add, and_out, bit_extender_2_out, bw1, bw2, div_hi, div_lo, hi_out, lo_out, lui, m_hi, m_lo,
       mult_hi, mult_lo, multiplexer_3_out, multiplexer_4_out, nor_1_out, or_out, shifter_2_out,
       shifter_3_out, shifter_5_out, shifter_6_out, sll, sllv, slt, sr_, sr_v, sub, xor_1_out;

  Shifter #(.width(32)) shifter_1 (.in(op1), .\dist (shift_amt), .out(sll));
  Shifter #(.width(32), .shift("lr")) shifter_2 (.in(op1), .\dist (shift_amt), .out(shifter_2_out));
  Multiplexer #(.width(32), .enable("false")) multiplexer_1 (
    .in0(shifter_2_out), .in1(shifter_3_out), .out(sr_), .sel(ALU_opcode[0]));
  Shifter #(.width(32), .shift("ar")) shifter_3 (.in(op1), .\dist (shift_amt), .out(shifter_3_out));
  Shifter #(.width(32)) shifter_4 (.in(op1), .\dist (op2[4:0]), .out(sllv));
  Shifter #(.width(32), .shift("lr")) shifter_5 (.in(op1), .\dist (op2[4:0]), .out(shifter_5_out));
  Multiplexer #(.width(32), .enable("false")) multiplexer_2 (
    .in0(shifter_5_out), .in1(shifter_6_out), .out(sr_v), .sel(ALU_opcode[0]));
  Shifter #(.width(32), .shift("ar")) shifter_6 (.in(op1), .\dist (op2[4:0]), .out(shifter_6_out));
  Multiplier #(.width(32)) multiplier_1 (.a(op1), .b(op2), .out(mult_lo), .cout(mult_hi));  // open: cin
  Divider #(.width(32)) divider_1 (.a(op1), .b(op2), .out(div_lo), .rem(div_hi));  // open: upper
  Multiplexer #(.select(2), .width(32), .enable("false")) multiplexer_3 (
    .in0(mult_hi), .in1(op1), .in2(div_hi), .out(multiplexer_3_out), .sel({mult, mthi}));  // open: in3
  Multiplexer #(.select(2), .width(32), .enable("false")) multiplexer_4 (
    .in0(mult_lo), .in1(op1), .in2(div_lo), .out(multiplexer_4_out), .sel({mult, mtlo}));  // open: in3
  Register #(.width(32)) hi (.D(multiplexer_3_out), .en(hi_en), .Q(hi_out), .clk(clk), .clr(rst));
  Register #(.width(32)) lo (.D(multiplexer_4_out), .en(lo_en), .Q(lo_out), .clk(clk), .clr(rst));
  add_flag add_flag_1 (.op1(op1), .op2(op2), .res(add), .v(add_v), .c(add_c));
  sub_flag sub_flag_1 (.op1(op1), .op2(op2), .res(sub), .v(sub_v), .c(sub_c));
  assign and_out = op1 & op2;  // AND_Gate and, 32 bits wide
  Multiplexer #(.width(32), .enable("false")) multiplexer_5 (
    .in0(and_out), .in1(or_out), .out(bw1), .sel(ALU_opcode[0]));
  assign or_out = op1 | op2;  // OR_Gate or, 32 bits wide
  assign xor_1_out = op1 ^ op2;  // XOR_Gate xor_1, 32 bits wide
  Multiplexer #(.width(32), .enable("false")) multiplexer_6 (
    .in0(xor_1_out), .in1(nor_1_out), .out(bw2), .sel(ALU_opcode[0]));
  assign nor_1_out = ~(op1 | op2);  // NOR_Gate nor_1, 32 bits wide
  Shifter #(.width(32)) shifter_7 (.in(op2), .\dist (5'b10000), .out(lui));
  Comparator #(.width(32)) comparator_1 (.a(op1), .b(op2), .lt(comparator_1_lt));  // open: gt, eq
  Multiplexer #(.enable("false")) multiplexer_7 (
    .in0(comparator_1_lt), .in1(comparator_2_lt), .out(multiplexer_7_out), .sel(ALU_opcode[0]));
  Comparator #(.width(32), .mode("unsigned")) comparator_2 (.a(op1), .b(op2), .lt(comparator_2_lt));  // open: gt, eq
  assign slt = {{31{1'b0}}, multiplexer_7_out};  // Bit_Extender bit_extender_1
  Comparator #(.width(32)) comparator_3 (.a(ALU_res), .b({32{1'b0}}), .eq(zero_flag));  // open: gt, lt
  Multiplexer #(.select(5), .width(32), .enable("false")) multiplexer_8 (
    .in0(sll), .in1(sr_), .in2(sllv), .in3(sr_v), .in4(op1), .in5({32{1'b0}}), .in6({32{1'b0}}),
    .in7({32{1'b0}}), .in8(m_hi), .in9(m_lo), .in10({32{1'b0}}), .in11({32{1'b0}}), .in12({32{1'b0}}),
    .in13({32{1'b0}}), .in14({32{1'b0}}), .in15({32{1'b0}}), .in16(add), .in17(sub), .in18(bw1), .in19(bw2),
    .in20(lui), .in21(slt), .in22({32{1'b0}}), .in23({32{1'b0}}), .in24({32{1'b0}}), .in25({32{1'b0}}),
    .in26({32{1'b0}}), .in27({32{1'b0}}), .in28({32{1'b0}}), .in29({32{1'b0}}), .in30({32{1'b0}}),
    .in31({32{1'b0}}), .out(ALU_res), .sel(ALU_opcode[5:1]));
  not not_1 (not_1_out, ALU_opcode[0]);
  Comparator #(.width(6)) comparator_4 (.a(ALU_opcode), .b(6'b010011), .eq(mtlo));  // open: gt, lt
  Comparator #(.width(5)) comparator_5 (.a(ALU_opcode[5:1]), .b(5'b01100), .eq(mult));  // open: gt, lt
  Comparator #(.width(5)) comparator_6 (.a(ALU_opcode[5:1]), .b(5'b01101), .eq(comparator_6_eq));  // open: gt, lt
  Comparator #(.width(6)) comparator_7 (.a(ALU_opcode), .b(6'b010001), .eq(mthi));  // open: gt, lt
  assign m_hi = hi_out & bit_extender_2_out;  // AND_Gate and_2, 32 bits wide
  assign bit_extender_2_out = {{31{not_1_out}}, not_1_out};  // Bit_Extender bit_extender_2
  assign m_lo = bit_extender_2_out & lo_out;  // AND_Gate and_3, 32 bits wide
  Multiplexer #(.disabled(0)) multiplexer_9 (
    .in0(add_v), .in1(sub_v), .out(overflow_flag), .sel(ALU_opcode[1]), .en(and_4_out));
  and and_4 (and_4_out, and_5_out, ~ALU_opcode[0]);  // AND_Gate
  and and_5 (and_5_out, ~ALU_opcode[2], ~ALU_opcode[3], ~ALU_opcode[4], ALU_opcode[5]);  // AND_Gate
  Multiplexer #(.disabled(0)) multiplexer_10 (
    .in0(add_c), .in1(sub_c), .out(carry_out), .sel(ALU_opcode[1]), .en(and_5_out));
  or or_2 (lo_en, mtlo, or_3_out);
  or or_3 (or_3_out, mult, comparator_6_eq);
  or or_4 (hi_en, or_3_out, mthi);

  // Other names for the same wires on the sheet: ALU_op[5:0] = ALU_opcode; ALUop_lsb = ALU_opcode[0];
  //   ALUop_msb5[4:0] = ALU_opcode[5:1]; cout_flag = carry_out; op_shamt[4:0] = op2[4:0]; ovf_flag = overflow_flag;
  //   shamt[4:0] = shift_amt
endmodule

module add_flag (
  input  [31:0] op1,
  input  [31:0] op2,
  output [31:0] res,
  output v,
  output c
);

  wire xor_1_out, xor_2_out;

  Adder #(.width(32)) adder_1 (.a(op1), .b(op2), .out(res), .cin(1'b0), .cout(c));
  xor xor_1 (xor_1_out, op1[31], res[31]);
  xor xor_2 (xor_2_out, res[31], op2[31]);
  and and_1 (v, xor_1_out, xor_2_out);

  // Other names for the same wires on the sheet: cout_flag = c; overflow_flag = v
endmodule

module sub_flag (
  input  [31:0] op1,
  input  [31:0] op2,
  output [31:0] res,
  output v,
  output c
);

  wire xor_1_out, xor_2_out;

  Subtractor #(.width(32)) subtractor_1 (.a(op1), .b(op2), .out(res), .bin(1'b0), .bout(c));
  xor xor_1 (xor_1_out, op1[31], res[31]);
  xor xor_2 (xor_2_out, res[31], ~op2[31]);  // XOR_Gate
  and and_1 (v, xor_1_out, xor_2_out);

  // Other names for the same wires on the sheet: cout_flag = c; overflow_flag = v
endmodule
