// Logisim project Register_File.circ as structural Verilog: 1 circuit, main circuit Register_bank
module Register_bank (
  input  [4:0] Rs,
  input  [4:0] Rt,
  input  [4:0] Rd,
  input  wr_en,
  input  [31:0] dest_data,
  input  clk,
  input  rst,
  input  [31:0] stack_start,
  input  [31:0] global_start,
  output [31:0] Rs_out,
  output [31:0] Rt_out
);

  wire _1_en, _2_en, _3_en, _4_en, _5_en, _6_en, _7_en, _8_en, _9_en, _10_en, _11_en, _12_en, _13_en, _14_en,
       _15_en, _16_en, _17_en, _18_en, _19_en, _20_en, _21_en, _22_en, _23_en, _24_en, _25_en, _26_en,
       _27_en, _28_en, _29_en, _30_en, _31_en;
  wire [31:0] a0, a1, a2, a3, at, fp, gp_t, k0, k1, ra, s0, s1, s2, s3, s4, s5, s6, s7, sp_t, t0, t1, t2, t3,
       t4, t5, t6, t7, t8, t9, v0, v1;

  Decoder #(.select(5), .disabled(0)) decoder_1 (
    .out1(_1_en), .out2(_2_en), .out3(_3_en), .out4(_4_en), .out5(_5_en), .out6(_6_en), .out7(_7_en),
    .out8(_8_en), .out9(_9_en), .out10(_10_en), .out11(_11_en), .out12(_12_en), .out13(_13_en),
    .out14(_14_en), .out15(_15_en), .out16(_16_en), .out17(_17_en), .out18(_18_en), .out19(_19_en),
    .out20(_20_en), .out21(_21_en), .out22(_22_en), .out23(_23_en), .out24(_24_en), .out25(_25_en),
    .out26(_26_en), .out27(_27_en), .out28(_28_en), .out29(_29_en), .out30(_30_en), .out31(_31_en), .sel(Rd),
    .en(wr_en));  // open: out0
  Register #(.width(32)) u_at (.D(dest_data), .en(_1_en), .Q(at), .clk(clk), .clr(rst));
  Register #(.width(32)) u_v0 (.D(dest_data), .en(_2_en), .Q(v0), .clk(clk), .clr(rst));
  Register #(.width(32)) u_v1 (.D(dest_data), .en(_3_en), .Q(v1), .clk(clk), .clr(rst));
  Register #(.width(32)) u_a0 (.D(dest_data), .en(_4_en), .Q(a0), .clk(clk), .clr(rst));
  Register #(.width(32)) u_a1 (.D(dest_data), .en(_5_en), .Q(a1), .clk(clk), .clr(rst));
  Register #(.width(32)) u_a2 (.D(dest_data), .en(_6_en), .Q(a2), .clk(clk), .clr(rst));
  Register #(.width(32)) u_a3 (.D(dest_data), .en(_7_en), .Q(a3), .clk(clk), .clr(rst));
  Register #(.width(32)) u_t0 (.D(dest_data), .en(_8_en), .Q(t0), .clk(clk), .clr(rst));
  Register #(.width(32)) u_t1 (.D(dest_data), .en(_9_en), .Q(t1), .clk(clk), .clr(rst));
  Register #(.width(32)) u_t2 (.D(dest_data), .en(_10_en), .Q(t2), .clk(clk), .clr(rst));
  Register #(.width(32)) u_t3 (.D(dest_data), .en(_11_en), .Q(t3), .clk(clk), .clr(rst));
  Register #(.width(32)) u_t4 (.D(dest_data), .en(_12_en), .Q(t4), .clk(clk), .clr(rst));
  Register #(.width(32)) u_t5 (.D(dest_data), .en(_13_en), .Q(t5), .clk(clk), .clr(rst));
  Register #(.width(32)) u_t6 (.D(dest_data), .en(_14_en), .Q(t6), .clk(clk), .clr(rst));
  Register #(.width(32)) u_t7 (.D(dest_data), .en(_15_en), .Q(t7), .clk(clk), .clr(rst));
  Register #(.width(32)) u_s0 (.D(dest_data), .en(_16_en), .Q(s0), .clk(clk), .clr(rst));
  Register #(.width(32)) u_s1 (.D(dest_data), .en(_17_en), .Q(s1), .clk(clk), .clr(rst));
  Register #(.width(32)) u_s2 (.D(dest_data), .en(_18_en), .Q(s2), .clk(clk), .clr(rst));
  Register #(.width(32)) u_s3 (.D(dest_data), .en(_19_en), .Q(s3), .clk(clk), .clr(rst));
  Register #(.width(32)) u_s4 (.D(dest_data), .en(_20_en), .Q(s4), .clk(clk), .clr(rst));
  Register #(.width(32)) u_s5 (.D(dest_data), .en(_21_en), .Q(s5), .clk(clk), .clr(rst));
  Register #(.width(32)) u_s6 (.D(dest_data), .en(_22_en), .Q(s6), .clk(clk), .clr(rst));
  Register #(.width(32)) u_s7 (.D(dest_data), .en(_23_en), .Q(s7), .clk(clk), .clr(rst));
  Register #(.width(32)) u_t8 (.D(dest_data), .en(_24_en), .Q(t8), .clk(clk), .clr(rst));
  Register #(.width(32)) u_t9 (.D(dest_data), .en(_25_en), .Q(t9), .clk(clk), .clr(rst));
  Register #(.width(32)) u_k0 (.D(dest_data), .en(_26_en), .Q(k0), .clk(clk), .clr(rst));
  Register #(.width(32)) u_k1 (.D(dest_data), .en(_27_en), .Q(k1), .clk(clk), .clr(rst));
  Register_Set gp (.D(dest_data), .S(global_start), .write_en(_28_en), .clk(clk), .rst(rst), .Q(gp_t));
  Register_Set sp (.D(dest_data), .S(stack_start), .write_en(_29_en), .clk(clk), .rst(rst), .Q(sp_t));
  Register #(.width(32)) u_fp (.D(dest_data), .en(_30_en), .Q(fp), .clk(clk), .clr(rst));
  Register #(.width(32)) u_ra (.D(dest_data), .en(_31_en), .Q(ra), .clk(clk), .clr(rst));
  Multiplexer #(.select(5), .width(32), .enable("false")) multiplexer_1 (
    .in0({32{1'b0}}), .in1(at), .in2(v0), .in3(v1), .in4(a0), .in5(a1), .in6(a2), .in7(a3), .in8(t0),
    .in9(t1), .in10(t2), .in11(t3), .in12(t4), .in13(t5), .in14(t6), .in15(t7), .in16(s0), .in17(s1),
    .in18(s2), .in19(s3), .in20(s4), .in21(s5), .in22(s6), .in23(s7), .in24(t8), .in25(t9), .in26(k0),
    .in27(k1), .in28(gp_t), .in29(sp_t), .in30(fp), .in31(ra), .out(Rs_out), .sel(Rs));
  Multiplexer #(.select(5), .width(32), .enable("false")) multiplexer_2 (
    .in0({32{1'b0}}), .in1(at), .in2(v0), .in3(v1), .in4(a0), .in5(a1), .in6(a2), .in7(a3), .in8(t0),
    .in9(t1), .in10(t2), .in11(t3), .in12(t4), .in13(t5), .in14(t6), .in15(t7), .in16(s0), .in17(s1),
    .in18(s2), .in19(s3), .in20(s4), .in21(s5), .in22(s6), .in23(s7), .in24(t8), .in25(t9), .in26(k0),
    .in27(k1), .in28(gp_t), .in29(sp_t), .in30(fp), .in31(ra), .out(Rt_out), .sel(Rt));

  // Other names for the same wires on the sheet: D[31:0] = dest_data; gp[31:0] = global_start; reg_dest[4:0] = Rd;
  //   reg_s[4:0] = Rs; reg_t[4:0] = Rt; sp[31:0] = stack_start
endmodule
