// Logisim project Register_Set.circ as structural Verilog: 1 circuit, main circuit Register_Set
module Register_Set (
  input  [31:0] D,
  input  [31:0] S,
  input  write_en,
  input  clk,
  input  rst,
  output [31:0] Q
);

  wire _30_q, _31_q, and_1_out, and_2_out, and_3_out, and_4_out, and_5_out, and_6_out, and_7_out, and_8_out,
       and_9_out, and_10_out, and_11_out, and_12_out, and_13_out, and_14_out, and_15_out, and_16_out,
       and_17_out, and_18_out, and_19_out, and_20_out, and_21_out, and_22_out, and_23_out, and_24_out,
       and_25_out, and_26_out, and_27_out, and_28_out, and_29_out, and_30_out, and_31_out, and_32_out,
       and_33_out, and_34_out, and_35_out, and_36_out, and_37_out, and_38_out, and_39_out, and_40_out,
       and_41_out, and_42_out, and_43_out, and_44_out, and_45_out, and_46_out, and_47_out, and_48_out,
       and_49_out, and_50_out, and_51_out, and_52_out, and_53_out, and_54_out, and_55_out, and_56_out,
       and_57_out, and_58_out, and_59_out, and_60_out, and_61_out, and_62_out, and_63_out, and_64_out;

  D_Flip_Flop d_ff_1 (.clk(clk), .D(D[0]), .Q(Q[0]), .preset(and_1_out), .en(write_en), .reset(and_2_out));  // open: Qn
  and and_1 (and_1_out, S[0], rst);
  and and_2 (and_2_out, ~S[0], rst);  // AND_Gate
  D_Flip_Flop d_ff_2 (.clk(clk), .D(D[1]), .Q(Q[1]), .preset(and_3_out), .en(write_en), .reset(and_4_out));  // open: Qn
  and and_3 (and_3_out, S[1], rst);
  and and_4 (and_4_out, ~S[1], rst);  // AND_Gate
  D_Flip_Flop d_ff_3 (.clk(clk), .D(D[2]), .Q(Q[2]), .preset(and_5_out), .en(write_en), .reset(and_6_out));  // open: Qn
  and and_5 (and_5_out, S[2], rst);
  and and_6 (and_6_out, ~S[2], rst);  // AND_Gate
  D_Flip_Flop d_ff_4 (.clk(clk), .D(D[3]), .Q(Q[3]), .preset(and_7_out), .en(write_en), .reset(and_8_out));  // open: Qn
  and and_7 (and_7_out, S[3], rst);
  and and_8 (and_8_out, ~S[3], rst);  // AND_Gate
  D_Flip_Flop d_ff_5 (
    .clk(clk), .D(D[4]), .Q(Q[4]), .preset(and_10_out), .en(write_en), .reset(and_9_out));  // open: Qn
  and and_9 (and_9_out, ~S[4], rst);  // AND_Gate
  and and_10 (and_10_out, S[4], rst);
  D_Flip_Flop d_ff_6 (
    .clk(clk), .D(D[5]), .Q(Q[5]), .preset(and_11_out), .en(write_en), .reset(and_12_out));  // open: Qn
  and and_11 (and_11_out, S[5], rst);
  and and_12 (and_12_out, ~S[5], rst);  // AND_Gate
  and and_13 (and_13_out, S[6], rst);
  and and_14 (and_14_out, S[7], rst);
  and and_15 (and_15_out, S[8], rst);
  and and_16 (and_16_out, S[9], rst);
  and and_17 (and_17_out, S[10], rst);
  and and_18 (and_18_out, S[11], rst);
  D_Flip_Flop d_ff_7 (
    .clk(clk), .D(D[6]), .Q(Q[6]), .preset(and_13_out), .en(write_en), .reset(and_19_out));  // open: Qn
  and and_19 (and_19_out, ~S[6], rst);  // AND_Gate
  D_Flip_Flop d_ff_8 (
    .clk(clk), .D(D[7]), .Q(Q[7]), .preset(and_14_out), .en(write_en), .reset(and_20_out));  // open: Qn
  and and_20 (and_20_out, ~S[7], rst);  // AND_Gate
  D_Flip_Flop d_ff_9 (
    .clk(clk), .D(D[8]), .Q(Q[8]), .preset(and_15_out), .en(write_en), .reset(and_21_out));  // open: Qn
  and and_21 (and_21_out, ~S[8], rst);  // AND_Gate
  D_Flip_Flop d_ff_10 (
    .clk(clk), .D(D[9]), .Q(Q[9]), .preset(and_16_out), .en(write_en), .reset(and_22_out));  // open: Qn
  and and_22 (and_22_out, ~S[9], rst);  // AND_Gate
  D_Flip_Flop d_ff_11 (
    .clk(clk), .D(D[10]), .Q(Q[10]), .preset(and_17_out), .en(write_en), .reset(and_23_out));  // open: Qn
  and and_23 (and_23_out, ~S[10], rst);  // AND_Gate
  D_Flip_Flop d_ff_12 (
    .clk(clk), .D(D[11]), .Q(Q[11]), .preset(and_18_out), .en(write_en), .reset(and_24_out));  // open: Qn
  and and_24 (and_24_out, ~S[11], rst);  // AND_Gate
  D_Flip_Flop d_ff_13 (
    .clk(clk), .D(D[12]), .Q(Q[12]), .preset(and_26_out), .en(write_en), .reset(and_25_out));  // open: Qn
  and and_25 (and_25_out, ~S[12], rst);  // AND_Gate
  and and_26 (and_26_out, S[12], rst);
  D_Flip_Flop d_ff_14 (
    .clk(clk), .D(D[13]), .Q(Q[13]), .preset(and_27_out), .en(write_en), .reset(and_28_out));  // open: Qn
  and and_27 (and_27_out, S[13], rst);
  and and_28 (and_28_out, ~S[13], rst);  // AND_Gate
  D_Flip_Flop d_ff_15 (
    .clk(clk), .D(D[14]), .Q(Q[14]), .preset(and_29_out), .en(write_en), .reset(and_30_out));  // open: Qn
  and and_29 (and_29_out, S[14], rst);
  and and_30 (and_30_out, ~S[14], rst);  // AND_Gate
  D_Flip_Flop d_ff_16 (
    .clk(clk), .D(D[15]), .Q(Q[15]), .preset(and_32_out), .en(write_en), .reset(and_31_out));  // open: Qn
  and and_31 (and_31_out, ~S[15], rst);  // AND_Gate
  and and_32 (and_32_out, S[15], rst);
  D_Flip_Flop d_ff_17 (
    .clk(clk), .D(D[16]), .Q(Q[16]), .preset(and_33_out), .en(write_en), .reset(and_34_out));  // open: Qn
  and and_33 (and_33_out, S[16], rst);
  and and_34 (and_34_out, ~S[16], rst);  // AND_Gate
  D_Flip_Flop d_ff_18 (
    .clk(clk), .D(D[17]), .Q(Q[17]), .preset(and_35_out), .en(write_en), .reset(and_36_out));  // open: Qn
  and and_35 (and_35_out, S[17], rst);
  and and_36 (and_36_out, ~S[17], rst);  // AND_Gate
  D_Flip_Flop d_ff_19 (
    .clk(clk), .D(D[18]), .Q(Q[18]), .preset(and_38_out), .en(write_en), .reset(and_37_out));  // open: Qn
  and and_37 (and_37_out, ~S[18], rst);  // AND_Gate
  and and_38 (and_38_out, S[18], rst);
  D_Flip_Flop d_ff_20 (
    .clk(clk), .D(D[19]), .Q(Q[19]), .preset(and_40_out), .en(write_en), .reset(and_39_out));  // open: Qn
  and and_39 (and_39_out, ~S[19], rst);  // AND_Gate
  and and_40 (and_40_out, S[19], rst);
  D_Flip_Flop d_ff_21 (
    .clk(clk), .D(D[20]), .Q(Q[20]), .preset(and_42_out), .en(write_en), .reset(and_41_out));  // open: Qn
  and and_41 (and_41_out, ~S[20], rst);  // AND_Gate
  and and_42 (and_42_out, S[20], rst);
  D_Flip_Flop d_ff_22 (
    .clk(clk), .D(D[21]), .Q(Q[21]), .preset(and_43_out), .en(write_en), .reset(and_44_out));  // open: Qn
  and and_43 (and_43_out, S[21], rst);
  and and_44 (and_44_out, ~S[21], rst);  // AND_Gate
  D_Flip_Flop d_ff_23 (
    .clk(clk), .D(D[22]), .Q(Q[22]), .preset(and_45_out), .en(write_en), .reset(and_46_out));  // open: Qn
  and and_45 (and_45_out, S[22], rst);
  and and_46 (and_46_out, ~S[22], rst);  // AND_Gate
  D_Flip_Flop d_ff_24 (
    .clk(clk), .D(D[23]), .Q(Q[23]), .preset(and_48_out), .en(write_en), .reset(and_47_out));  // open: Qn
  and and_47 (and_47_out, ~S[23], rst);  // AND_Gate
  and and_48 (and_48_out, S[23], rst);
  and and_49 (and_49_out, S[24], rst);
  and and_50 (and_50_out, S[25], rst);
  and and_51 (and_51_out, S[26], rst);
  and and_52 (and_52_out, S[27], rst);
  and and_53 (and_53_out, S[28], rst);
  and and_54 (and_54_out, S[29], rst);
  D_Flip_Flop d_ff_25 (
    .clk(clk), .D(D[24]), .Q(Q[24]), .preset(and_49_out), .en(write_en), .reset(and_55_out));  // open: Qn
  and and_55 (and_55_out, ~S[24], rst);  // AND_Gate
  D_Flip_Flop d_ff_26 (
    .clk(clk), .D(D[25]), .Q(Q[25]), .preset(and_50_out), .en(write_en), .reset(and_56_out));  // open: Qn
  and and_56 (and_56_out, ~S[25], rst);  // AND_Gate
  D_Flip_Flop d_ff_27 (
    .clk(clk), .D(D[26]), .Q(Q[26]), .preset(and_51_out), .en(write_en), .reset(and_57_out));  // open: Qn
  and and_57 (and_57_out, ~S[26], rst);  // AND_Gate
  D_Flip_Flop d_ff_28 (
    .clk(clk), .D(D[27]), .Q(Q[27]), .preset(and_52_out), .en(write_en), .reset(and_58_out));  // open: Qn
  and and_58 (and_58_out, ~S[27], rst);  // AND_Gate
  D_Flip_Flop d_ff_29 (
    .clk(clk), .D(D[28]), .Q(Q[28]), .preset(and_53_out), .en(write_en), .reset(and_59_out));  // open: Qn
  and and_59 (and_59_out, ~S[28], rst);  // AND_Gate
  D_Flip_Flop d_ff_30 (
    .clk(clk), .D(D[29]), .Q(Q[29]), .preset(and_54_out), .en(write_en), .reset(and_60_out));  // open: Qn
  and and_60 (and_60_out, ~S[29], rst);  // AND_Gate
  D_Flip_Flop d_ff_31 (
    .clk(clk), .D(D[30]), .Q(_30_q), .preset(and_61_out), .en(write_en), .reset(and_62_out));  // open: Qn
  and and_61 (and_61_out, S[30], rst);
  and and_62 (and_62_out, ~S[30], rst);  // AND_Gate
  D_Flip_Flop d_ff_32 (
    .clk(clk), .D(D[31]), .Q(_31_q), .preset(and_63_out), .en(write_en), .reset(and_64_out));  // open: Qn
  and and_63 (and_63_out, S[31], rst);
  and and_64 (and_64_out, ~S[31], rst);  // AND_Gate

  assign Q[31:30] = D[31:30];

  // Other names for the same wires on the sheet: _0_d = D[0]; _1_d = D[1]; _2_d = D[2]; _3_d = D[3]; _4_d = D[4];
  //   _5_d = D[5]; _6_d = D[6]; _7_d = D[7]; _8_d = D[8]; _9_d = D[9]; _10_d = D[10]; _11_d = D[11]; _12_d = D[12];
  //   _13_d = D[13]; _14_d = D[14]; _15_d = D[15]; _16_d = D[16]; _17_d = D[17]; _18_d = D[18]; _19_d = D[19];
  //   _20_d = D[20]; _21_d = D[21]; _22_d = D[22]; _23_d = D[23]; _24_d = D[24]; _25_d = D[25]; _26_d = D[26];
  //   _27_d = D[27]; _28_d = D[28]; _29_d = D[29]; _0_q = Q[0]; _1_q = Q[1]; _2_q = Q[2]; _3_q = Q[3]; _4_q = Q[4];
  //   _5_q = Q[5]; _6_q = Q[6]; _7_q = Q[7]; _8_q = Q[8]; _9_q = Q[9]; _10_q = Q[10]; _11_q = Q[11]; _12_q = Q[12];
  //   _13_q = Q[13]; _14_q = Q[14]; _15_q = Q[15]; _16_q = Q[16]; _17_q = Q[17]; _18_q = Q[18]; _19_q = Q[19];
  //   _20_q = Q[20]; _21_q = Q[21]; _22_q = Q[22]; _23_q = Q[23]; _24_q = Q[24]; _25_q = Q[25]; _26_q = Q[26];
  //   _27_q = Q[27]; _28_q = Q[28]; _29_q = Q[29]; _30_d = D[30]; _31_d = D[31]; _0_s = S[0]; _1_s = S[1];
  //   _2_s = S[2]; _3_s = S[3]; _4_s = S[4]; _5_s = S[5]; _6_s = S[6]; _7_s = S[7]; _8_s = S[8]; _9_s = S[9];
  //   _10_s = S[10]; _11_s = S[11]; _12_s = S[12]; _13_s = S[13]; _14_s = S[14]; _15_s = S[15]; _16_s = S[16];
  //   _17_s = S[17]; _18_s = S[18]; _19_s = S[19]; _20_s = S[20]; _21_s = S[21]; _22_s = S[22]; _23_s = S[23];
  //   _24_s = S[24]; _25_s = S[25]; _26_s = S[26]; _27_s = S[27]; _28_s = S[28]; _29_s = S[29]; _30_s = S[30];
  //   _31_s = S[31]; wr_en = write_en
endmodule
